# Fritzing sketch meveo (saved by Fritzing 0.7.11b)
breadboards: 1

parts:
  LED = LED - 5mm [color="Red (633nm)" package="5 mm [THT]"]
  Pull_Down_Resistor_(100_KOhm) = Resistor [tolerance=±5% resistance=100k package=THT]
  Switch = Pushbutton [package="[THT]"]
  LED_Resistor_(470_Ohm) = Resistor [tolerance=±5% resistance=470 package=THT]
  Arduino1 = Arduino

nets:
  N1: LED.cathode, Pull_Down_Resistor_(100_KOhm).Pin_0, Arduino1.GND
  N2: LED.anode, LED_Resistor_(470_Ohm).Pin_0
  N3: Pull_Down_Resistor_(100_KOhm).Pin_1, Switch.Pin_3, Switch.Pin_4, LED_Resistor_(470_Ohm).Pin_1, Arduino1.D4
  N4: Switch.Pin_1, Switch.Pin_2, Arduino1.+5V
